# Fritzing sketch basement_sensor (saved by Fritzing 0.9.3b)
circuit board: 8.46667cm x 5.64444cm
breadboards: 1

parts:
  Part1 = Adafruit HUZZAH32 ESP32 Feather [part_number="Adafruit #3405"]
  AM1 = AM2302 Humidity and Temperature Sensor

nets:
  N1: Part1.IO21, AM1.DATA
  GND: Part1.GND, AM1.GND
  N2: Part1.VBUS, AM1.VDD
